# Fritzing sketch arduino_ir_receiver (saved by Fritzing 0.8.3b)
breadboards: 1

parts:
  IR1 = TSOP312.., 314.. [part_number=TSOP382 package=THT]
  C1 = Electrolytic Capacitor [capacitance=1μF package="0405 [SMD, electrolytic]"]
  LED1 = LED - 5mm [color="Red (633nm)" package="5 mm [THT]"]
  LED2 = LED - 5mm [color="Green (555nm)" package="5 mm [THT]"]
  R1 = Resistor [tolerance=±5% resistance=47 package=THT]
  IC1 = IC, DIP package, 8 pins [chip_label=MCP4131 part_number="Microchip MCP4131"]
  Photocell_CdS = PHOTOCELL [package=photocell]
  R3 = Resistor [tolerance=±5% resistance=10k package=THT]
  R4 = Resistor [tolerance=±5% resistance=220 package=THT]
  R5 = Resistor [tolerance=±5% resistance=220 package=THT]
  IC3 = IC, DIP package, 8 pins [chip_label=MCP4131 part_number="Microchip MCP4131"]
  Part1 = Arduino Micro (Rev3)

nets:
  GND: IR1.GND, C1.-, IC1.pin4, IC1.pin7, R3.Pin_0, R4.Pin_0, R5.Pin_0, IC3.pin4, IC3.pin7, Part1.GND
  5V: IR1.Vs, C1.+, R1.Pin_0, R1.Pin_1, IC1.pin5, IC1.pin8, Photocell_CdS.P$2, IC3.pin8, Part1.5V
  N1: IR1.Data, Part1.D9_PWM/A9
  N2: LED1.cathode, R5.Pin_1
  N3: LED1.anode, IC3.pin6
  N4: LED2.cathode, R4.Pin_1
  N5: LED2.anode, IC1.pin6
  N6: IC1.pin1, Part1.D10_PWM/A10
  N7: IC1.pin2, IC3.pin2, Part1.SCK
  N8: IC1.pin3, IC3.pin3, Part1.MOSI
  N9: Photocell_CdS.P$1, R3.Pin_1, Part1.A0
  N10: IC3.pin1, Part1.D11_PWM
  N11: IC3.pin5, Part1.D12_PWM/A11
